# Fritzing sketch circuit-diagram (saved by Fritzing 0.9.3b)
breadboards: 1

parts:
  Part1 = Arduino Mega 2560 (Rev3)
  DRV_1 = DRV 8825 Stepper Motor Carrier, High Current [part_number="DRV 8825"]  # not connected
  C1 = Electrolytic Capacitor [capacitance=100µF package="100 mil [THT, electrolytic]"]
  Power_plug1 = Power plug [part_number="12v Power Source"]
  M1 = Stepper Motor - Bipolar  # not connected

nets:
  GND: Part1.GND, C1.+, Power_plug1.GND
  VIN: Part1.VIN, C1.-, Power_plug1.VCC

notes:
  12 volt input
